// Logisim project fpu_circuito.circ as structural Verilog: 1 circuit, main circuit main
module main (
  input  ADD_SUB
);

  Clock clock_1 ();  // open: out
  Multiplexer multiplexer_1 ();  // open: in0, in1, out, sel, en
  Adder adder_1 ();  // open: a, b, out, cin, cout
  Multiplexer multiplexer_2 ();  // open: in0, in1, out, sel, en
  Subtractor subtractor_1 ();  // open: a, b, out, bin, bout

  // Notes on the sheet:
  //   Unidade de ponto flutuante FPU
endmodule
